# Fritzing sketch Placa cableado (saved by Fritzing 0.9.3b)
circuit board: 4.1cm x 2.62cm
breadboards: 1

parts:
  FSR = Basic Force Sensing Resistor (FSR) [package=THT]
  Dout = Header 1 [package=1x01_offset]
  FSR_2 = Header 1 [package=1x01_offset]
  JP3 = Header 1 [package=1x01_offset]
  JP1 = Header 1 [package=1x01_offset]
  JP2 = Header 1 [package=1x01_offset]
  R1 = Resistor [tolerance=±5% resistance=1k package=THT]
  Din = Header 1 [package=1x01_offset]
  +LED = Header 1 [package=1x01_offset]
  +FSR = Header 1 [package=1x01_offset]
  GND = Header 1 [package=1x01_offset]
  4 = Header 1 [package=1x01_offset]
  3 = Header 1 [package=1x01_offset]
  2 = Header 1 [package=1x01_offset]
  1 = Header 1 [package=1x01_offset]
  4_2 = Header 1 [package=1x01_offset]  # not connected
  +FSR_2 = Header 1 [package=1x01_offset]
  +LED_2 = Header 1 [package=1x01_offset]
  GND_2 = Header 1 [package=1x01_offset]
  Dout_2 = Header 1 [package=1x01_offset]
  3_2 = Header 1 [package=1x01_offset]
  2_2 = Header 1 [package=1x01_offset]
  1_2 = Header 1 [package=1x01_offset]
  +LED_3 = Header 1 [package=1x01_offset]
  GND_3 = Header 1 [package=1x01_offset]
  Din_2 = Header 1 [package=1x01_offset]
  C1 = Ceramic Capacitor [capacitance=100nF package="100 mil [THT, multilayer]"]
  C2 = Ceramic Capacitor [capacitance="100 nF" package="0603 [SMD, multilayer]"]
  C3 = Electrolytic Capacitor [capacitance=1µF package="100 mil [THT, electrolytic]"]  # not connected
  Din1 = Header 1 [package=1x01_offset]
  Din2 = Header 1 [package=1x01_offset]

nets:
  N1: FSR.pin_0, JP1.1
  N2: FSR.pin_1, JP2.1
  N3: Dout.1, Dout_2.1
  N4: FSR_2.1, R1.Pin_0, 1.1, C1.0, C2.1
  N5: JP3.1, GND.1, GND_2.1, GND_3.1, C1.1, C2.0, Din2.1
  N6: R1.Pin_1, +FSR.1, +FSR_2.1
  N7: Din.1, Din_2.1
  N8: +LED.1, +LED_2.1, +LED_3.1, Din1.1
  N9: 4.1, 3_2.1
  N10: 3.1, 2_2.1
  N11: 2.1, 1_2.1

notes:
  Hacia arduino
  OUT
  IN
